# Fritzing sketch Robotic Arm Electronics (saved by Fritzing 0.9.10b)

parts:
  Jetson_Nano1 = jetsonnano
  Part1 = 16-Channel 12-bit PWM Servo Driver - I2C [part_number=815]
  DC1 = DC_DC_XL4016 [package=board_screw]
  L1 = Solenoid  # not connected
  U1 = 640x480 CMOS Color Camera [package=camera_cmos_plug]  # not connected
  U2 = Battery Holders [package=lipo-1100mAh]
  U3 = Battery Holders [package=lipo-1100mAh]
  U4 = Battery Holders [package=lipo-1100mAh]
  J1 = Basic Servo
  J2 = Basic Servo
  J3 = Basic Servo
  J4 = Basic Servo
  J5 = Basic Servo
  Q1 = NPN-Transistor [package="TO92 [THT]"]  # not connected

nets:
  N1: Jetson_Nano1.connector20, Part1.VCC
  N2: Jetson_Nano1.connector21, Part1.SCL
  N3: Jetson_Nano1.connector22, Part1.SDA
  GND: Jetson_Nano1.connector39, Part1.GND, DC1.OUT-, J1.gnd, J2.gnd, J3.gnd, J4.gnd, J5.gnd
  N4: Part1.PWRIN, DC1.OUT+
  N5: Part1.PWM4, J1.pulse
  VCC: Part1.5.0V, J1.vcc, J2.vcc, J3.vcc, J4.vcc, J5.vcc
  N6: Part1.PWM3, J4.pulse
  N7: Part1.PWM2, J5.pulse
  N8: Part1.PWM1, J3.pulse
  N9: Part1.PWM0, J2.pulse
  N10: DC1.IN+, U4.+
  N11: DC1.IN-, U2.-
  N12: U2.+, U3.-
  N13: U3.+, U4.-

custom parts:
  16-Channel 12-bit PWM Servo Driver - I2C: You want to make a cool robot, maybe a hexapod walker, or maybe just a piece of art with a lot of moving parts. Or maybe you want to drive a lot of LEDs with precise PWM output. Using only two pins, control 16 free-running PWM outputs! You can even chain up 62 breakouts to control up to 992 PWM outputs.
  DC_DC_XL4016: DC-DC Converter step down voltage regulator XL4016 custom sketch.
